# Fritzing sketch dim-led (saved by Fritzing 0.9.3b)
breadboards: 1

parts:
  Raspberry_Pi_1 = Raspberry Pi 3 [part_number=RPI-3-V1.2]
  LED1 = LED - 5mm [color="Green (570nm)" package="5 mm [THT]"]
  R1 = Resistor [tolerance=±5% resistance=220 package=THT]
  LED2 = LED - 5mm [color="Yellow (595nm)" package="5 mm [THT]"]
  R2 = Resistor [tolerance=±5% resistance=220 package=THT]

nets:
  N1: Raspberry_Pi_1.GIPO12, LED2.cathode
  N2: Raspberry_Pi_1.GIPO18, LED1.cathode
  N3: Raspberry_Pi_1.GND, R1.Pin_0, R2.Pin_0
  N4: LED1.anode, R1.Pin_1
  N5: LED2.anode, R2.Pin_1
